// Logisim project partial-load.circ as structural Verilog: 1 circuit, main circuit partial_load
module partial_load (
  input  [31:0] Instruction,
  input  [31:0] MemAddress,
  input  [31:0] DataFromMem,
  output [31:0] DataToReg
);

  wire and_1_out, and_2_out, and_3_out, and_4_out, and_5_out, and_6_out, and_7_out, and_8_out, and_9_out,
       and_10_out, and_11_out, comparator_1_eq, comparator_2_eq, comparator_3_eq, comparator_4_eq,
       comparator_5_eq, comparator_6_eq, comparator_7_eq, comparator_8_eq, comparator_9_eq, comparator_10_eq,
       comparator_11_eq, comparator_12_eq;
  wire [2:0] priority_encoder_1_out;
  wire [16:0] bit_extender_5_out, bit_extender_6_out, bit_extender_7_out;
  wire [24:0] bit_extender_1_out, bit_extender_2_out, bit_extender_3_out, bit_extender_4_out;

  Comparator #(.width(7)) comparator_1 (.a(Instruction[6:0]), .b(7'b0000011), .eq(comparator_1_eq));  // open: gt, lt
  Comparator #(.width(3)) comparator_2 (.a(Instruction[14:12]), .b(3'b000), .eq(comparator_2_eq));  // open: gt, lt
  Comparator #(.width(3)) comparator_3 (.a(Instruction[14:12]), .b(3'b001), .eq(comparator_3_eq));  // open: gt, lt
  Comparator #(.width(3)) comparator_4 (.a(Instruction[14:12]), .b(3'b010), .eq(comparator_4_eq));  // open: gt, lt
  assign bit_extender_1_out = {{24{DataFromMem[7]}}, DataFromMem[7]};  // Bit_Extender bit_extender_1
  assign bit_extender_2_out = {{24{DataFromMem[15]}}, DataFromMem[15]};  // Bit_Extender bit_extender_2
  assign bit_extender_3_out = {{24{DataFromMem[23]}}, DataFromMem[23]};  // Bit_Extender bit_extender_3
  assign bit_extender_4_out = {{24{DataFromMem[31]}}, DataFromMem[31]};  // Bit_Extender bit_extender_4
  assign bit_extender_5_out = {{16{DataFromMem[15]}}, DataFromMem[15]};  // Bit_Extender bit_extender_5
  assign bit_extender_6_out = {{16{DataFromMem[31]}}, DataFromMem[31]};  // Bit_Extender bit_extender_6
  assign bit_extender_7_out = {{16{DataFromMem[23]}}, DataFromMem[23]};  // Bit_Extender bit_extender_7
  and and_1 (and_1_out, comparator_1_eq, comparator_2_eq);
  and and_2 (and_2_out, comparator_1_eq, comparator_3_eq);
  and and_3 (and_3_out, comparator_1_eq, comparator_4_eq);
  Comparator #(.width(2)) comparator_5 (.a(MemAddress[1:0]), .b(2'b00), .eq(comparator_5_eq));  // open: gt, lt
  Comparator #(.width(2)) comparator_6 (.a(MemAddress[1:0]), .b(2'b01), .eq(comparator_6_eq));  // open: gt, lt
  Comparator #(.width(2)) comparator_7 (.a(MemAddress[1:0]), .b(2'b10), .eq(comparator_7_eq));  // open: gt, lt
  Comparator #(.width(2)) comparator_8 (.a(MemAddress[1:0]), .b(2'b11), .eq(comparator_8_eq));  // open: gt, lt
  Comparator #(.width(2)) comparator_9 (.a(MemAddress[1:0]), .b(2'b00), .eq(comparator_9_eq));  // open: gt, lt
  Comparator #(.width(2)) comparator_10 (.a(MemAddress[1:0]), .b(2'b01), .eq(comparator_10_eq));  // open: gt, lt
  Comparator #(.width(2)) comparator_11 (.a(MemAddress[1:0]), .b(2'b10), .eq(comparator_11_eq));  // open: gt, lt
  Comparator #(.width(2)) comparator_12 (.a(MemAddress[1:0]), .b(2'b00), .eq(comparator_12_eq));  // open: gt, lt
  and and_4 (and_4_out, and_1_out, comparator_5_eq);
  and and_5 (and_5_out, and_1_out, comparator_6_eq);
  and and_6 (and_6_out, and_1_out, comparator_7_eq);
  and and_7 (and_7_out, and_1_out, comparator_8_eq);
  and and_8 (and_8_out, and_2_out, comparator_9_eq);
  and and_9 (and_9_out, and_2_out, comparator_10_eq);
  and and_10 (and_10_out, and_2_out, comparator_11_eq);
  and and_11 (and_11_out, and_3_out, comparator_12_eq);
  Multiplexer #(.select(3), .width(32)) multiplexer_1 (
    .in0({bit_extender_1_out, DataFromMem[6:0]}), .in1({bit_extender_2_out, DataFromMem[14:8]}),
    .in2({bit_extender_3_out, DataFromMem[22:16]}), .in3({bit_extender_4_out, DataFromMem[30:24]}),
    .in4({bit_extender_5_out, DataFromMem[14:0]}), .in5({bit_extender_7_out, DataFromMem[22:8]}),
    .in6({bit_extender_6_out, DataFromMem[30:16]}), .in7(DataFromMem), .out(DataToReg),
    .sel(priority_encoder_1_out));
  Priority_Encoder priority_encoder_1 (
    .in0(and_4_out), .in1(and_5_out), .in2(and_6_out), .in3(and_7_out), .in4(and_8_out), .in5(and_9_out),
    .in6(and_10_out), .in7(and_11_out), .out(priority_encoder_1_out));  // open: en_in, gs, en_out

  // Other names for the same wires on the sheet: opcode[6:0] = Instruction[6:0]; fun3[2:0] = Instruction[14:12];
  //   b2[1:0] = MemAddress[1:0]

  // Notes on the sheet:
  //   INPUTS to your circuit
  //   DON'T CHANGE THE LOCATIONS OF THE INPUTS AND OUTPUTS!
  //   OUTPUT from your circuit
endmodule
